# Fritzing sketch isolatedNodes (saved by Fritzing 0.9.4)
breadboards: 1

parts:
  Componente1 = Arduino Nano (Rev3.0)
  Componente2 = InvenSense MPU6050
  R4 = Resistor [tolerance=±5% resistance=220 package="1206 [SMD]"]
  ZS-042_RTC1 = ZS-042 RTC Module
  S8 = Pushbutton [package="[SMD]"]
  microSD1 = MicroSD Card Module
  R5 = Resistor [tolerance=±5% resistance=1k package="1206 [SMD]"]
  LED2 = LED - 5mm [color="Red (633nm)" package="5 mm [THT]"]
  R6 = Resistor [tolerance=±5% resistance=220 package="1206 [SMD]"]
  R7 = Resistor [tolerance=±5% resistance=220 package="1206 [SMD]"]
  R8 = Resistor [tolerance=±5% resistance=470 package="1206 [SMD]"]

nets:
  GND: Componente1.GND, Componente2.GND, ZS-042_RTC1.GND, microSD1.GND, R5.Pin_1, LED2.cathode, R6.Pin_1, R7.Pin_1, R8.Pin_1
  N1: Componente1.D2, R4.Pin_0, R4.Pin_1, LED2.anode
  N2: Componente1.D4, microSD1.CS
  N3: Componente1.D7, R8.Pin_0
  N4: Componente1.D8, S8.Pin_3, S8.Pin_4, R5.Pin_0
  N5: Componente1.D9, R6.Pin_0
  N6: Componente1.D10, R7.Pin_0
  N7: Componente1.D11/MOSI, microSD1.MOSI
  N8: Componente1.D12/MISO, microSD1.MISO
  VCC: Componente1.5V, Componente2.VCC, Componente2.AD0, ZS-042_RTC1.VCC, S8.Pin_1, S8.Pin_2, microSD1.VCC
  N9: Componente1.A5, Componente2.SCL, ZS-042_RTC1.SCL
  N10: Componente1.A4, Componente2.SDA, ZS-042_RTC1.SDA
  N11: Componente1.D13/SCK, microSD1.SCK

custom parts:
  MicroSD Card Module: A common microSD card module.
