# Fritzing sketch cabledNodes (saved by Fritzing 0.9.4)
breadboards: 1

parts:
  Componente1 = Arduino Nano (Rev3.0)
  Componente2 = InvenSense MPU6050
  R4 = Resistor [tolerance=±5% resistance=220 package="1206 [SMD]"]
  ZS-042_RTC1 = ZS-042 RTC Module
  S8 = Pushbutton [package="[SMD]"]
  microSD1 = MicroSD Card Module
  R5 = Resistor [tolerance=±5% resistance=1k package="1206 [SMD]"]
  LED2 = LED - 5mm [color="Red (633nm)" package="5 mm [THT]"]
  RS485_module1 = RS485 Module (MAX3485)
  R9 = Resistor [tolerance=±5% resistance=470 package="1206 [SMD]"]
  R10 = Resistor [tolerance=±5% resistance=220 package="1206 [SMD]"]
  R11 = Resistor [tolerance=±5% resistance=220 package="1206 [SMD]"]
  RS485_module2 = RS485 Module (MAX3485)

nets:
  GND: Componente1.GND, Componente2.GND, ZS-042_RTC1.GND, microSD1.GND, R5.Pin_1, LED2.cathode, RS485_module1.GND, R9.Pin_1, R10.Pin_1, R11.Pin_1
  N1: Componente1.D2, R4.Pin_0, R4.Pin_1, LED2.anode
  N2: Componente1.D3, RS485_module1.RE, RS485_module1.DE
  N3: Componente1.D4, microSD1.CS
  N4: Componente1.D5, RS485_module1.RO
  N5: Componente1.D6, RS485_module1.DI
  N6: Componente1.D7, R9.Pin_0
  N7: Componente1.D8, S8.Pin_3, S8.Pin_4, R5.Pin_0
  N8: Componente1.D9, R10.Pin_0
  N9: Componente1.D10, R11.Pin_0
  N10: Componente1.D11/MOSI, microSD1.MOSI
  N11: Componente1.D12/MISO, microSD1.MISO
  VCC: Componente1.5V, Componente2.VCC, Componente2.AD0, ZS-042_RTC1.VCC, S8.Pin_1, S8.Pin_2, microSD1.VCC, RS485_module1.VCC
  N12: Componente1.A5, Componente2.SCL, ZS-042_RTC1.SCL
  N13: Componente1.A4, Componente2.SDA, ZS-042_RTC1.SDA
  N14: Componente1.D13/SCK, microSD1.SCK
  N15: RS485_module1.A, RS485_module2.A
  N16: RS485_module1.B, RS485_module2.B

custom parts:
  MicroSD Card Module: A common microSD card module.
  RS485 Module (MAX3485): Commercially available RS485 to RS232 TTL Module
