# Fritzing sketch wirelessNodes (saved by Fritzing 0.9.4)
breadboards: 1

parts:
  Componente1 = Arduino Nano (Rev3.0)
  Componente2 = InvenSense MPU6050
  R4 = Resistor [tolerance=±5% resistance=220 package="1206 [SMD]"]
  ZS-042_RTC1 = ZS-042 RTC Module
  microSD1 = MicroSD Card Module
  R5 = Resistor [tolerance=±5% resistance=1k package="1206 [SMD]"]
  LEDA1 = LED - 5mm [color="Red (633nm)" package="5 mm [THT]"]
  R10 = Resistor [tolerance=±5% resistance=220 package="1206 [SMD]"]
  R11 = Resistor [tolerance=±5% resistance=220 package="1206 [SMD]"]
  Componente4 = NRF24L01+ Breakout Board
  LEDA0 = LED - 5mm [color="Green (570nm)" package="5 mm [THT]"]
  R12 = Resistor [tolerance=±5% resistance=220 package="1206 [SMD]"]
  Botao1 = Pushbutton [package="[SMD]"]
  R13 = Resistor [tolerance=±5% resistance=1k package="1206 [SMD]"]
  R14 = Resistor [tolerance=±5% resistance=220 package="1206 [SMD]"]
  R15 = Resistor [tolerance=±5% resistance=220 package="1206 [SMD]"]
  R16 = Resistor [tolerance=±5% resistance=470 package="1206 [SMD]"]
  R17 = Resistor [tolerance=±5% resistance=470 package="1206 [SMD]"]
  Botao2 = Pushbutton [package="[SMD]"]

nets:
  GND: Componente1.GND, Componente2.GND, ZS-042_RTC1.GND, microSD1.GND, R5.Pin_1, LEDA1.cathode, R10.Pin_1, R11.Pin_1, Componente4.GND, LEDA0.cathode, R13.Pin_1, R14.Pin_1, R15.Pin_1
  N1: Componente1.D2, Botao1.Pin_3, Botao1.Pin_4, R13.Pin_0
  N2: Componente1.D3, R5.Pin_0, Botao2.Pin_3, Botao2.Pin_4
  N3: Componente1.D4, microSD1.CS
  N4: Componente1.D5, R15.Pin_0
  N5: Componente1.D6, R14.Pin_0
  N6: Componente1.D7, Componente4.CE
  N7: Componente1.D8, Componente4.CS
  N8: Componente1.D9, R10.Pin_0
  N9: Componente1.D10, R11.Pin_0
  N10: Componente1.D11/MOSI, microSD1.MOSI, Componente4.MOSI
  N11: Componente1.D12/MISO, microSD1.MISO, Componente4.MISO
  VCC: Componente1.5V, Componente2.VCC, Componente2.AD0, ZS-042_RTC1.VCC, microSD1.VCC, Componente4.VCC, Botao1.Pin_1, Botao1.Pin_2, R16.Pin_0, R17.Pin_0, Botao2.Pin_1, Botao2.Pin_2
  N12: Componente1.A7, R16.Pin_1
  N13: Componente1.A5, Componente2.SCL, ZS-042_RTC1.SCL
  N14: Componente1.A4, Componente2.SDA, ZS-042_RTC1.SDA
  N15: Componente1.A2, R17.Pin_1
  N16: Componente1.A1, R4.Pin_0, R4.Pin_1, LEDA1.anode
  N17: Componente1.A0, LEDA0.anode, R12.Pin_0, R12.Pin_1
  N18: Componente1.D13/SCK, microSD1.SCK, Componente4.SCK

custom parts:
  MicroSD Card Module: A common microSD card module.
